# Fritzing sketch mecanum sketch (saved by Fritzing 1.0.3b)
circuit board: 16.4702cm x 10.7999cm
breadboards: 1

parts:
  Arduino_Base = Arduino Uno (Rev3)
  Motor_Shield = Adafruit Motor/Stepper/Servo Shield [part_number="Adafruit #1438"]
  A3 = Esp32-c3 super mini
  HC-SR04_Sensor_1 = HC-SR04 Ultrasonic Distance Sensor

nets:
  N1: Arduino_Base.A0, Motor_Shield.AD0
  N2: Arduino_Base.A1, Motor_Shield.AD1
  N3: Arduino_Base.A2, Motor_Shield.AD2
  N4: Arduino_Base.A3, Motor_Shield.AD3
  N5: Arduino_Base.A4/SDA, Motor_Shield.AD4/SDA
  N6: Arduino_Base.A5/SCL, Motor_Shield.AD5/SCL
  N7: Arduino_Base.D8, Motor_Shield.D8
  N8: Arduino_Base.D9_PWM, Motor_Shield.D9
  N9: Arduino_Base.D10_PWM/SS, Motor_Shield.D10
  N10: Arduino_Base.D11_PWM/MOSI, Motor_Shield.D11
  N11: Arduino_Base.D12/MISO, Motor_Shield.D12
  N12: Arduino_Base.D13/SCK, Motor_Shield.D13
  GND: Arduino_Base.GND, Motor_Shield.GND, A3.Pin_15, HC-SR04_Sensor_1.GND
  N13: Arduino_Base.AREF, Motor_Shield.AREF
  N14: Arduino_Base.D0/RX, Motor_Shield.D0, A3.Pin_7
  N15: Arduino_Base.D1/TX, Motor_Shield.D1, A3.Pin_8
  N16: Arduino_Base.D2, Motor_Shield.D2
  N17: Arduino_Base.D3_PWM, Motor_Shield.D3
  N18: Arduino_Base.D4, Motor_Shield.D4
  N19: Arduino_Base.D5_PWM, Motor_Shield.D5
  N20: Arduino_Base.D6_PWM, Motor_Shield.D6
  N21: Arduino_Base.D7, Motor_Shield.D7
  N22: Arduino_Base.ioref, Motor_Shield.IOREF
  N23: Arduino_Base.RESET, Motor_Shield./RST
  3V3: Arduino_Base.3V3, Motor_Shield.+3V3
  5V: Arduino_Base.5V, Motor_Shield.+5V, A3.Pin_16, HC-SR04_Sensor_1.VCC
  VIN: Arduino_Base.VIN, Motor_Shield.VIN
  N24: A3.Pin_12, HC-SR04_Sensor_1.ECHO
  N25: A3.Pin_14, HC-SR04_Sensor_1.TRIG

notes:
  Blue TX
  Yellow RX

custom parts:
  Adafruit Motor/Stepper/Servo Shield: The original Adafruit Motorshield kit is one of our most beloved kits, which is why we decided to make something even better. We have upgraded the shield kit to make the bestest, easiest way to drive DC and Stepper motors. This shield will make quick work of your next robotics project! We kept the ability to drive up to 4 DC motors or 2 stepper motors, but added many improvements: Instead of a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
  Esp32-c3 super mini: ESP32-C3 Development Board ESP32 SuperMini Development Board ESP32 Development Board WiFi Bluetooth.
